// Logisim project number4.circ as structural Verilog: 1 circuit, main circuit main
module main (
  input  A,
  input  in_2,
  output D0,
  output D1,
  output out_5,
  output D3
);

  wire not_1_out, not_2_out;

  not not_1 (not_1_out, A);
  not not_2 (not_2_out, in_2);
  and and_1 (D0, not_1_out, not_2_out);
  and and_2 (D1, not_1_out, in_2);
  and and_3 (out_5, A, not_2_out);
  and and_4 (D3, A, in_2);

  // Notes on the sheet:
  //   B
  //   D2
endmodule
